# Fritzing sketch schematic (saved by Fritzing 0.9.10b)
breadboards: 1

parts:
  Part1 = Arduino Uno (Rev3) - ICSP  # not connected
  HC-SR04_Sensor_1 = HC-SR04 Ultrasonic Distance Sensor
  LCD1 = LCD screen
  Part2 = Memoire 1.0 - SD card log shield
  Part3 = 16x8 LED Matrix Backpack [part_number=2039]
  Part4 = Adafruit I2C+SPI LCD Backpack [part_number="Adafruit #292"]
  J2 = Basic Servo [part_number=MG995]
  BATT1 = 4xAA Switchable Battery Pack w/Bare Wire
  SP1 = SPEAKER [package=pcb_mount_speaker]  # not connected
  J4 = Basic Servo [part_number=S51]
  J5 = Basic Servo [part_number=S51]
  J6 = Basic Servo [part_number=MG995]
  S1 = Toggle Switch [package=THT]

nets:
  VCC: HC-SR04_Sensor_1.VCC, LCD1.VDD, LCD1.LED+, Part2.+5V, Part3.VDD, Part4.VCC
  N1: HC-SR04_Sensor_1.TRIG, Part2.DIG_9
  N2: HC-SR04_Sensor_1.ECHO, Part2.DIG_8
  GND: HC-SR04_Sensor_1.GND, LCD1.VSS, LCD1.R/W, Part2.GND, Part3.GND, Part4.GND, J2.gnd, BATT1.NEG, J4.gnd, J5.gnd, J6.gnd
  N3: LCD1.V0, Part4.CONTRAST
  N4: LCD1.RS, Part4.RS
  N5: LCD1.E, Part4.E
  N6: LCD1.DB0, Part4.DB0
  N7: LCD1.DB1, Part4.DB1
  N8: LCD1.DB2, Part4.DB2
  N9: LCD1.DB3, Part4.DB3
  N10: LCD1.DB4, Part4.DB4
  N11: LCD1.DB5, Part4.DB5
  N12: LCD1.DB6, Part4.DB6
  N13: LCD1.DB7, Part4.DB7
  N14: LCD1.LED-, Part4.LEDK
  N15: Part2.DIG_10, Part2.DIG_2, Part2.DIG_4, Part2.DIG_0
  N16: Part2.DIG_3, Part2.DIG_5, Part2.DIG_1
  N17: Part2.A_IN_0, J4.pulse
  N18: Part2.A_IN_1, J5.pulse
  N19: Part2.A_IN_2, J2.pulse
  N20: Part2.A_IN_3, J6.pulse
  N21: Part2.A_IN_4, Part3.SDA, Part4.DATA
  N22: Part2.A_IN_5, Part3.SCL, Part4.CLOCK
  VCC_2: J2.vcc, J4.vcc, J5.vcc, J6.vcc, S1.COM
  N23: BATT1.POS, S1.L2

notes:
  Not the waveshield I used (from adafruit) but shown wired in that way.
  2 -> LCS
  3 -> CLK
  4 -> DI
  5 -> LAT
  10 -> CCS
  connected to the waveshield at audio-out

custom parts:
  16x8 LED Matrix Backpack: This 16x8 monochrome LED matrix includes a driver chip for simple control via an I2C interface. The backpack features address-selection jumpers so you can connect up to eight matrices on a single I2C bus.
  Adafruit I2C+SPI LCD Backpack: LCD backpacks reduce the number of pins needed to connect to an LCD. LCDs are a fun and easy way to have your microcontroller project talk back to you. Character LCDs are common, and easy to get, available in tons of colors and sizes. We've written tutorials on using character LCDs with an Arduino (or similar microcontroller) but find that the number of pins necessary to control the LCD can be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
  4xAA Switchable Battery Pack w/Bare Wire: 4xAA Switchable Battery Pack with Bare Wire connection
